// Logisim project 16BitsAdder.circ as structural Verilog: 4 circuits, main circuit halfAdder
module halfAdder (
  input  A,
  input  B,
  output S,
  output CO
);

  xor xor_1 (S, A, B);
  and and_1 (CO, A, B);
endmodule

module fullAdder (
  input  CI,
  input  A,
  input  B,
  output S,
  output CO
);

  wire halfadder_1_co, halfadder_1_s, halfadder_2_co;

  halfAdder halfadder_1 (.A(A), .B(B), .S(halfadder_1_s), .CO(halfadder_1_co));
  halfAdder halfadder_2 (.A(CI), .B(halfadder_1_s), .S(S), .CO(halfadder_2_co));
  or or_1 (CO, halfadder_2_co, halfadder_1_co);
endmodule

module adderSubtractor8Bits (
  input  M,
  input  A0,
  input  B0,
  input  A1,
  input  B1,
  input  A2,
  input  B2,
  input  A3,
  input  B3,
  input  A4,
  input  B4,
  input  A5,
  input  B5,
  input  A6,
  input  B6,
  input  A7,
  input  B7,
  input  A0_2,
  input  B0_2,
  input  A1_2,
  input  B1_2,
  input  A2_2,
  input  B2_2,
  input  A3_2,
  input  B3_2,
  input  A4_2,
  input  B4_2,
  input  A5_2,
  input  B5_2,
  input  A6_2,
  input  B6_2,
  input  A7_2,
  input  B7_2,
  output S0,
  output S1,
  output S2,
  output S3,
  output S4,
  output S5,
  output S6,
  output S7,
  output out_42,
  output S1_2,
  output S2_2,
  output S3_2,
  output S4_2,
  output S5_2,
  output S6_2,
  output S7_2,
  output C7
);

  wire fulladder_1_co, fulladder_2_co, fulladder_3_co, fulladder_4_co, fulladder_5_co, fulladder_6_co,
       fulladder_7_co, fulladder_8_co, fulladder_9_co, fulladder_10_co, fulladder_11_co, fulladder_12_co,
       fulladder_13_co, fulladder_14_co, fulladder_15_co, xor_1_out, xor_2_out, xor_3_out, xor_4_out,
       xor_5_out, xor_6_out, xor_7_out, xor_8_out, xor_9_out, xor_10_out, xor_11_out, xor_12_out, xor_13_out,
       xor_14_out, xor_15_out, xor_16_out;

  fullAdder fulladder_1 (.CI(M), .A(A0), .B(xor_1_out), .S(S0), .CO(fulladder_1_co));
  xor xor_1 (xor_1_out, B0, M);
  fullAdder fulladder_2 (.CI(fulladder_1_co), .A(A1), .B(xor_2_out), .S(S1), .CO(fulladder_2_co));
  xor xor_2 (xor_2_out, B1, M);
  fullAdder fulladder_3 (.CI(fulladder_2_co), .A(A2), .B(xor_3_out), .S(S2), .CO(fulladder_3_co));
  xor xor_3 (xor_3_out, B2, M);
  fullAdder fulladder_4 (.CI(fulladder_3_co), .A(A3), .B(xor_4_out), .S(S3), .CO(fulladder_4_co));
  xor xor_4 (xor_4_out, B3, M);
  fullAdder fulladder_5 (.CI(fulladder_4_co), .A(A4), .B(xor_5_out), .S(S4), .CO(fulladder_5_co));
  xor xor_5 (xor_5_out, B4, M);
  fullAdder fulladder_6 (.CI(fulladder_5_co), .A(A5), .B(xor_6_out), .S(S5), .CO(fulladder_6_co));
  xor xor_6 (xor_6_out, B5, M);
  fullAdder fulladder_7 (.CI(fulladder_6_co), .A(A6), .B(xor_7_out), .S(S6), .CO(fulladder_7_co));
  xor xor_7 (xor_7_out, B6, M);
  fullAdder fulladder_8 (.CI(fulladder_7_co), .A(A7), .B(xor_8_out), .S(S7), .CO(fulladder_8_co));
  xor xor_8 (xor_8_out, B7, M);
  fullAdder fulladder_9 (.CI(fulladder_8_co), .A(A0_2), .B(xor_9_out), .S(out_42), .CO(fulladder_9_co));
  xor xor_9 (xor_9_out, B0_2, M);
  fullAdder fulladder_10 (.CI(fulladder_9_co), .A(A1_2), .B(xor_10_out), .S(S1_2), .CO(fulladder_10_co));
  xor xor_10 (xor_10_out, B1_2, M);
  fullAdder fulladder_11 (.CI(fulladder_10_co), .A(A2_2), .B(xor_11_out), .S(S2_2), .CO(fulladder_11_co));
  xor xor_11 (xor_11_out, B2_2, M);
  fullAdder fulladder_12 (.CI(fulladder_11_co), .A(A3_2), .B(xor_12_out), .S(S3_2), .CO(fulladder_12_co));
  xor xor_12 (xor_12_out, B3_2, M);
  fullAdder fulladder_13 (.CI(fulladder_12_co), .A(A4_2), .B(xor_13_out), .S(S4_2), .CO(fulladder_13_co));
  xor xor_13 (xor_13_out, B4_2, M);
  fullAdder fulladder_14 (.CI(fulladder_13_co), .A(A5_2), .B(xor_14_out), .S(S5_2), .CO(fulladder_14_co));
  xor xor_14 (xor_14_out, B5_2, M);
  fullAdder fulladder_15 (.CI(fulladder_14_co), .A(A6_2), .B(xor_15_out), .S(S6_2), .CO(fulladder_15_co));
  xor xor_15 (xor_15_out, B6_2, M);
  fullAdder fulladder_16 (.CI(fulladder_15_co), .A(A7_2), .B(xor_16_out), .S(S7_2), .CO(C7));
  xor xor_16 (xor_16_out, B7_2, M);
endmodule

module adderSubtractor16Bits (
  input  M0,
  input  in_2,
  input  in_3,
  input  in_4,
  input  in_5,
  input  in_6,
  input  in_7,
  input  in_8,
  input  in_9,
  input  in_10,
  input  in_11,
  input  in_12,
  input  in_13,
  input  in_14,
  input  in_15,
  input  in_16,
  input  in_17,
  input  in_18,
  input  in_19,
  input  in_20,
  input  in_21,
  input  in_22,
  input  in_23,
  input  in_24,
  input  in_25,
  input  in_26,
  input  in_27,
  input  in_28,
  input  in_29,
  input  in_30,
  input  in_31,
  input  in_32,
  input  in_33,
  output out_34,
  output out_35,
  output out_36,
  output out_37,
  output out_38,
  output out_39,
  output out_40,
  output out_41,
  output out_42,
  output out_43,
  output out_44,
  output out_45,
  output out_46,
  output out_47,
  output out_48,
  output out_49
);

  adderSubtractor8Bits addersubtractor8bits_1 (
    .B1(M0), .A2(in_2), .B2(in_3), .A3(in_4), .B3(in_5), .A4(in_6), .B4(in_7), .A5(in_8), .B5(in_9),
    .A6(in_10), .B6(in_11), .A7(in_12), .B7(in_13), .A0_2(in_14), .B0_2(in_15), .A1_2(in_16), .B1_2(in_17),
    .S0(out_34), .S1(out_35), .S2(out_36), .S3(out_37), .S4(out_38), .S5(out_39), .S6(out_40), .S7(out_41));  // open: M, A0, B0, A1, A2_2, B2_2, A3_2, B3_2, A4_2, B4_2, A5_2, B5_2, A6_2, B6_2, A7_2, B7_2, out_42, S1_2, S2_2, S3_2, S4_2, S5_2, S6_2, S7_2, C7
  adderSubtractor8Bits addersubtractor8bits_2 (
    .B0(M0), .B1(M0), .A2(in_18), .B2(in_19), .A3(in_20), .B3(in_21), .A4(in_22), .B4(in_23), .A5(in_24),
    .B5(in_25), .A6(in_26), .B6(in_27), .A7(in_28), .B7(in_29), .A0_2(in_30), .B0_2(in_31), .A1_2(in_32),
    .B1_2(in_33), .S0(out_42), .S1(out_43), .S2(out_44), .S3(out_45), .S4(out_46), .S5(out_47), .S6(out_48),
    .S7(out_49));  // open: M, A0, A1, A2_2, B2_2, A3_2, B3_2, A4_2, B4_2, A5_2, B5_2, A6_2, B6_2, A7_2, B7_2, out_42, S1_2, S2_2, S3_2, S4_2, S5_2, S6_2, S7_2, C7
endmodule
