// Logisim project 16BitsAdderSubtractor.circ as structural Verilog: 3 circuits, main circuit halfAdder
module halfAdder (
  input  A,
  input  B,
  output S,
  output CO
);

  xor xor_1 (S, A, B);
  and and_1 (CO, A, B);
endmodule

module fullAdder (
  input  CI,
  input  A,
  input  B,
  output S,
  output CO
);

  wire halfadder_1_co, halfadder_1_s, halfadder_2_co;

  halfAdder halfadder_1 (.A(A), .B(B), .S(halfadder_1_s), .CO(halfadder_1_co));
  halfAdder halfadder_2 (.A(CI), .B(halfadder_1_s), .S(S), .CO(halfadder_2_co));
  or or_1 (CO, halfadder_2_co, halfadder_1_co);
endmodule

module adderSubtractor16Bits (
  input  M,
  input  A0,
  input  B0,
  input  A1,
  input  B1,
  input  A2,
  input  B2,
  input  A3,
  input  B3,
  input  A4,
  input  B4,
  input  A5,
  input  B5,
  input  A6,
  input  B6,
  input  A7,
  input  B7,
  input  A8,
  input  B8,
  input  A9,
  input  B9,
  input  A10,
  input  B10,
  input  A11,
  input  B11,
  input  A12,
  input  B12,
  input  A13,
  input  B13,
  input  A14,
  input  B14,
  input  A15,
  input  B15,
  output S0,
  output S1,
  output S2,
  output S3,
  output S4,
  output S5,
  output S6,
  output S7,
  output S8,
  output S9,
  output S10,
  output S11,
  output S12,
  output S13,
  output S14,
  output S15,
  output C15
);

  wire fulladder_1_co, fulladder_2_co, fulladder_3_co, fulladder_4_co, fulladder_5_co, fulladder_6_co,
       fulladder_7_co, fulladder_8_co, fulladder_9_co, fulladder_10_co, fulladder_11_co, fulladder_12_co,
       fulladder_13_co, fulladder_14_co, fulladder_15_co, xor_1_out, xor_2_out, xor_3_out, xor_4_out,
       xor_5_out, xor_6_out, xor_7_out, xor_8_out, xor_9_out, xor_10_out, xor_11_out, xor_12_out, xor_13_out,
       xor_14_out, xor_15_out, xor_16_out;

  fullAdder fulladder_1 (.CI(M), .A(A0), .B(xor_1_out), .S(S0), .CO(fulladder_1_co));
  xor xor_1 (xor_1_out, B0, M);
  fullAdder fulladder_2 (.CI(fulladder_1_co), .A(A1), .B(xor_2_out), .S(S1), .CO(fulladder_2_co));
  xor xor_2 (xor_2_out, B1, M);
  fullAdder fulladder_3 (.CI(fulladder_2_co), .A(A2), .B(xor_3_out), .S(S2), .CO(fulladder_3_co));
  xor xor_3 (xor_3_out, B2, M);
  fullAdder fulladder_4 (.CI(fulladder_3_co), .A(A3), .B(xor_4_out), .S(S3), .CO(fulladder_4_co));
  xor xor_4 (xor_4_out, B3, M);
  fullAdder fulladder_5 (.CI(fulladder_4_co), .A(A4), .B(xor_5_out), .S(S4), .CO(fulladder_5_co));
  xor xor_5 (xor_5_out, B4, M);
  fullAdder fulladder_6 (.CI(fulladder_5_co), .A(A5), .B(xor_6_out), .S(S5), .CO(fulladder_6_co));
  xor xor_6 (xor_6_out, B5, M);
  fullAdder fulladder_7 (.CI(fulladder_6_co), .A(A6), .B(xor_7_out), .S(S6), .CO(fulladder_7_co));
  xor xor_7 (xor_7_out, B6, M);
  fullAdder fulladder_8 (.CI(fulladder_7_co), .A(A7), .B(xor_8_out), .S(S7), .CO(fulladder_8_co));
  xor xor_8 (xor_8_out, B7, M);
  fullAdder fulladder_9 (.CI(fulladder_8_co), .A(A8), .B(xor_9_out), .S(S8), .CO(fulladder_9_co));
  xor xor_9 (xor_9_out, B8, M);
  fullAdder fulladder_10 (.CI(fulladder_9_co), .A(A9), .B(xor_10_out), .S(S9), .CO(fulladder_10_co));
  xor xor_10 (xor_10_out, B9, M);
  fullAdder fulladder_11 (.CI(fulladder_10_co), .A(A10), .B(xor_11_out), .S(S10), .CO(fulladder_11_co));
  xor xor_11 (xor_11_out, B10, M);
  fullAdder fulladder_12 (.CI(fulladder_11_co), .A(A11), .B(xor_12_out), .S(S11), .CO(fulladder_12_co));
  xor xor_12 (xor_12_out, B11, M);
  fullAdder fulladder_13 (.CI(fulladder_12_co), .A(A12), .B(xor_13_out), .S(S12), .CO(fulladder_13_co));
  xor xor_13 (xor_13_out, B12, M);
  fullAdder fulladder_14 (.CI(fulladder_13_co), .A(A13), .B(xor_14_out), .S(S13), .CO(fulladder_14_co));
  xor xor_14 (xor_14_out, B13, M);
  fullAdder fulladder_15 (.CI(fulladder_14_co), .A(A14), .B(xor_15_out), .S(S14), .CO(fulladder_15_co));
  xor xor_15 (xor_15_out, B14, M);
  fullAdder fulladder_16 (.CI(fulladder_15_co), .A(A15), .B(xor_16_out), .S(S15), .CO(C15));
  xor xor_16 (xor_16_out, B15, M);
endmodule
