// Logisim project 16_bits_adder_subtractor.circ as structural Verilog: 3 circuits, main circuit half_adder
module half_adder (
  input  A,
  input  B,
  output S,
  output CO
);

  xor xor_1 (S, A, B);
  and and_1 (CO, A, B);
endmodule

module full_adder (
  input  CI,
  input  A,
  input  B,
  output S,
  output CO
);

  wire half_adder_1_co, half_adder_1_s, half_adder_2_co;

  half_adder half_adder_1 (.A(A), .B(B), .S(half_adder_1_s), .CO(half_adder_1_co));
  half_adder half_adder_2 (.A(CI), .B(half_adder_1_s), .S(S), .CO(half_adder_2_co));
  or or_1 (CO, half_adder_2_co, half_adder_1_co);
endmodule

module adder_subtractor (
  input  M,
  input  A0,
  input  B0,
  input  A1,
  input  B1,
  input  A2,
  input  B2,
  input  A3,
  input  B3,
  input  A4,
  input  B4,
  input  A5,
  input  B5,
  input  A6,
  input  B6,
  input  A7,
  input  B7,
  input  A8,
  input  B8,
  input  A9,
  input  B9,
  input  A10,
  input  B10,
  input  A11,
  input  B11,
  input  A12,
  input  B12,
  input  A13,
  input  B13,
  input  A14,
  input  B14,
  input  A15,
  input  B15,
  output S0,
  output S1,
  output S2,
  output S3,
  output S4,
  output S5,
  output S6,
  output S7,
  output S8,
  output S9,
  output S10,
  output S11,
  output S12,
  output S13,
  output S14,
  output S15,
  output C15
);

  wire full_adder_1_co, full_adder_2_co, full_adder_3_co, full_adder_4_co, full_adder_5_co, full_adder_6_co,
       full_adder_7_co, full_adder_8_co, full_adder_9_co, full_adder_10_co, full_adder_11_co,
       full_adder_12_co, full_adder_13_co, full_adder_14_co, full_adder_15_co, xor_1_out, xor_2_out,
       xor_3_out, xor_4_out, xor_5_out, xor_6_out, xor_7_out, xor_8_out, xor_9_out, xor_10_out, xor_11_out,
       xor_12_out, xor_13_out, xor_14_out, xor_15_out, xor_16_out;

  full_adder full_adder_1 (.CI(M), .A(A0), .B(xor_1_out), .S(S0), .CO(full_adder_1_co));
  xor xor_1 (xor_1_out, B0, M);
  full_adder full_adder_2 (.CI(full_adder_1_co), .A(A1), .B(xor_2_out), .S(S1), .CO(full_adder_2_co));
  xor xor_2 (xor_2_out, B1, M);
  full_adder full_adder_3 (.CI(full_adder_2_co), .A(A2), .B(xor_3_out), .S(S2), .CO(full_adder_3_co));
  xor xor_3 (xor_3_out, B2, M);
  full_adder full_adder_4 (.CI(full_adder_3_co), .A(A3), .B(xor_4_out), .S(S3), .CO(full_adder_4_co));
  xor xor_4 (xor_4_out, B3, M);
  full_adder full_adder_5 (.CI(full_adder_4_co), .A(A4), .B(xor_5_out), .S(S4), .CO(full_adder_5_co));
  xor xor_5 (xor_5_out, B4, M);
  full_adder full_adder_6 (.CI(full_adder_5_co), .A(A5), .B(xor_6_out), .S(S5), .CO(full_adder_6_co));
  xor xor_6 (xor_6_out, B5, M);
  full_adder full_adder_7 (.CI(full_adder_6_co), .A(A6), .B(xor_7_out), .S(S6), .CO(full_adder_7_co));
  xor xor_7 (xor_7_out, B6, M);
  full_adder full_adder_8 (.CI(full_adder_7_co), .A(A7), .B(xor_8_out), .S(S7), .CO(full_adder_8_co));
  xor xor_8 (xor_8_out, B7, M);
  full_adder full_adder_9 (.CI(full_adder_8_co), .A(A8), .B(xor_9_out), .S(S8), .CO(full_adder_9_co));
  xor xor_9 (xor_9_out, B8, M);
  full_adder full_adder_10 (.CI(full_adder_9_co), .A(A9), .B(xor_10_out), .S(S9), .CO(full_adder_10_co));
  xor xor_10 (xor_10_out, B9, M);
  full_adder full_adder_11 (.CI(full_adder_10_co), .A(A10), .B(xor_11_out), .S(S10), .CO(full_adder_11_co));
  xor xor_11 (xor_11_out, B10, M);
  full_adder full_adder_12 (.CI(full_adder_11_co), .A(A11), .B(xor_12_out), .S(S11), .CO(full_adder_12_co));
  xor xor_12 (xor_12_out, B11, M);
  full_adder full_adder_13 (.CI(full_adder_12_co), .A(A12), .B(xor_13_out), .S(S12), .CO(full_adder_13_co));
  xor xor_13 (xor_13_out, B12, M);
  full_adder full_adder_14 (.CI(full_adder_13_co), .A(A13), .B(xor_14_out), .S(S13), .CO(full_adder_14_co));
  xor xor_14 (xor_14_out, B13, M);
  full_adder full_adder_15 (.CI(full_adder_14_co), .A(A14), .B(xor_15_out), .S(S14), .CO(full_adder_15_co));
  xor xor_15 (xor_15_out, B14, M);
  full_adder full_adder_16 (.CI(full_adder_15_co), .A(A15), .B(xor_16_out), .S(S15), .CO(C15));
  xor xor_16 (xor_16_out, B15, M);
endmodule
